# Fritzing sketch wiring (saved by Fritzing 0.9.3b)

parts:
  Bauteil1 = Arduino Pro Mini (3.3V)
  Config-Taster = Momentary Switch [package=ksa_sealed_tac_switch]
  LED = LED - 3mm [color="Green (560nm)" package="3 mm [THT]"]
  R1 = Resistor [tolerance=±5% resistance=330 package=THT]
  part = CC1101 [part_number=CC1101]
  SDS1 = SDS011 - dust sensor [part_number=1]
  5V = Power Jack [package=power_jack_slot]

nets:
  N1: Bauteil1.A4, SDS1.TX
  N2: Bauteil1.A5, SDS1.RX
  N3: Bauteil1.RAW, SDS1.5v, 5V.PWR
  GND: Bauteil1.GND, Config-Taster.4, LED.cathode, part.2, SDS1.GND, 5V.GND
  N4: Bauteil1.VCC, part.1
  N5: Bauteil1.SCK, part.4
  N6: Bauteil1.MISO, part.5
  N7: Bauteil1.MOSI, part.3
  N8: Bauteil1.D10, part.8
  N9: Bauteil1.D8, Config-Taster.3
  N10: Bauteil1.D4, R1.Pin_0
  N11: Bauteil1.D2, part.7
  N12: LED.anode, R1.Pin_1

custom parts:
  SDS011 - dust sensor: The SDS 011 Sensor is a quite recent Air Quality Sensor developed by inovafit, a spin-off from the university of Jinan (in Shandong). With its size, it is probably one of the best sensor in terms of accuracy: While other sensors tend to focus on shrinking the sensor size, the SDS 011 has opted for a size tradeoff allowing it to use a larger fan. And the larger the fan, the better the quality.
